# Fritzing sketch ESQUEMA ARDUINO (saved by Fritzing 0.8.7b)
breadboards: 1

parts:
  Parte1 = Arduino Uno (Rev3)
  R1 = Resistor [tolerance=±5% resistance=10k package=THT]
  R2 = Resistor [tolerance=±5% resistance=10k package=THT]
  R3 = Resistor [tolerance=±5% resistance=10k package=THT]
  R4 = Resistor [tolerance=±5% resistance=220 package=THT]
  R5 = Resistor [tolerance=±5% resistance=220 package=THT]
  R6 = Resistor [tolerance=±5% resistance=220 package=THT]
  S1 = Pushbutton [package="[THT]"]
  S2 = Pushbutton [package="[THT]"]
  S3 = Pushbutton [package="[THT]"]
  LED1 = RGB LED (com. anode, rbg) [package="5 mm [THT]"]

nets:
  N1: Parte1.D9_PWM, R5.Pin_1
  N2: Parte1.D10_PWM/SS, R6.Pin_1
  N3: Parte1.D11_PWM/MOSI, R4.Pin_1
  N4: Parte1.D2, R3.Pin_0, S3.Pin_1, S3.Pin_2
  N5: Parte1.D3_PWM, R2.Pin_0, S2.Pin_3, S2.Pin_4
  N6: Parte1.D4, R1.Pin_0, S1.Pin_3, S1.Pin_4
  N7: Parte1.5V, S1.Pin_1, S1.Pin_2, S2.Pin_1, S2.Pin_2, S3.Pin_3, S3.Pin_4
  N8: Parte1.GND, R1.Pin_1, R2.Pin_1, R3.Pin_1, LED1.common_anode
  N9: R4.Pin_0, LED1.red_cathode
  N10: R5.Pin_0, LED1.green_cathode
  N11: R6.Pin_0, LED1.blue_cathode
